# Fritzing sketch circuit (saved by Fritzing 0.9.1b)
breadboards: 1

parts:
  Componente1 = Arduino Nano (Rev3.0)
  Drive_1 = screw terminal, 3 pins
  Drive_2 = screw terminal, 3 pins
  Drive_3 = screw terminal, 3 pins
  Drive_4 = screw terminal, 3 pins
  Drive_5 = screw terminal, 3 pins
  12v = Screw terminal - 2 pins [package=THT]

nets:
  N1: Componente1.D1/TX, Drive_5.pin1
  N2: Componente1.D0/RX, Drive_5.pin2
  N3: Componente1.GND, Drive_1.pin3, Drive_2.pin3, Drive_3.pin3, Drive_4.pin3, Drive_5.pin3, 12v.pin2
  N4: Componente1.D2, Drive_4.pin2
  N5: Componente1.D3, Drive_4.pin1
  N6: Componente1.D4, Drive_3.pin2
  N7: Componente1.D5, Drive_3.pin1
  N8: Componente1.D6, Drive_2.pin2
  N9: Componente1.D7, Drive_2.pin1
  N10: Componente1.D8, Drive_1.pin2
  N11: Componente1.D9, Drive_1.pin1
  N12: Componente1.VIN, 12v.pin1
